# Fritzing sketch tplink_fernsteuerung_1 (saved by Fritzing 0.9.4)
breadboards: 2

parts:
  Part1 = SRF05 Ultrasonic Rangefinder
  R1 = Resistor [tolerance=±5% resistance=2.2k package=THT]
  R2 = Resistor [tolerance=±5% resistance=1k package=THT]
  OLED1 = OLED 128x64 I2C Monochrome Display GND-VDD
  S1 = Pushbutton [package="[THT]"]
  LED1 = LED - 5mm [color="Red (633nm)" package="5 mm [THT]"]
  LED2 = LED - 5mm [color="Yellow (592nm)" package="5 mm [THT]"]
  ADC1 = MCP3008 [package=dil16]
  R4 = Resistor [tolerance=±1% resistance=1k package=THT]
  R5 = Resistor [tolerance=±1% resistance=330 package=THT]
  R6 = Resistor [tolerance=±1% resistance=330 package=THT]
  MCU1 = Raspberry Pi Zero
  Raspberry_Pi_1 = Raspberry Pi 4 [part_number=RPI-4-b]

nets:
  VCC: Part1.VCC, Raspberry_Pi_1.5V
  N1: Part1.Trig, Raspberry_Pi_1.GPIO16
  N2: Part1.Echo, R2.Pin_1
  GND: Part1.GND, R1.Pin_1, OLED1.GND, Raspberry_Pi_1.GND
  N3: R1.Pin_0, R2.Pin_0, Raspberry_Pi_1.GPIO26
  VDD: OLED1.VDD, Raspberry_Pi_1.3V3
  N4: OLED1.SCK, Raspberry_Pi_1.GPIO3
  N5: OLED1.SDA, Raspberry_Pi_1.GPIO2
  N6: S1.Pin_1, S1.Pin_2, LED1.cathode, LED2.cathode, ADC1.DGND, ADC1.AGND, MCU1.pin_6, MCU1.pin_9, MCU1.pin_39
  N7: S1.Pin_3, S1.Pin_4, R4.Pin_1
  N8: LED1.anode, R6.Pin_1
  N9: LED2.anode, R5.Pin_1
  N10: ADC1.CS/SHDN, MCU1.pin_24
  N11: ADC1.Din, MCU1.pin_19
  N12: ADC1.Dout, MCU1.pin_21
  N13: ADC1.CLK, MCU1.pin_23
  N14: ADC1.VREF, ADC1.VDD
  N15: R4.Pin_0, MCU1.pin_13
  N16: R5.Pin_0, MCU1.pin_11
  N17: R6.Pin_0, MCU1.pin_16

notes:
  HC-SR04
  AZDelivery 0,96 Zoll OLED Display I2C 128 x 64 Pixel

custom parts:
  OLED 128x64 I2C Monochrome Display GND-VDD: OLED 128x64 I2C Monochrome Display. Note: there are two variants of this part, this one is the GND VDD SCK SDA variant. The other is VDD GND SCK SDA. Make sure you select the part that matches your module as using the incorrect part will probably destroy your module! In addition the mounting holes are marked on silkscreen but not by default drilled. If you want drilled mounting holes, copy a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
  Raspberry Pi 4: The RPi4, a faster version of the awesome Raspberry Pi 2 B ARM Board with 40 pin gpio. Ready for special Raspberry Pi B+ and RPi2 Hat (Hardware attached (on) top)
